# Fritzing sketch Schematics (saved by Fritzing 0.9.3b)

parts:
  7_4V_2200mAH_LiPo_Battery = LIPO-2000mAh [package=lipo-2000]
  Arduino_Uno_WiFi_Rev_2 = Arduino Uno (Rev3)
  ESC = SO08w [chip_label=ESC package=SO(w)]
  PDB = SO14w [chip_label="Power Distribution Board" package=SO(w)]
  Brushless_Motor = Basic Servo
  R1 = Resistor [tolerance=±1% resistance=10k package="1206 [SMD]"]
  R2 = Resistor [tolerance=±1% resistance=10k package="1206 [SMD]"]
  U1 = SWITCH-SPST-2 [package=switch-spst-vertical]

nets:
  N1: 7_4V_2200mAH_LiPo_Battery.+, U1.O
  N2: 7_4V_2200mAH_LiPo_Battery.-, PDB.13
  N3: Arduino_Uno_WiFi_Rev_2.A0, R1.Pin_0, R2.Pin_1
  N4: Arduino_Uno_WiFi_Rev_2.D6_PWM, ESC.2
  N5: Arduino_Uno_WiFi_Rev_2.5V, ESC.1
  N6: Arduino_Uno_WiFi_Rev_2.VIN, ESC.3
  N7: ESC.4, PDB.7
  N8: ESC.5, Brushless_Motor.gnd
  N9: ESC.6, Brushless_Motor.pulse
  N10: ESC.7, Brushless_Motor.vcc
  N11: ESC.8, PDB.6
  N12: PDB.1, R2.Pin_0
  N13: PDB.2, R1.Pin_1
  N14: PDB.14, U1.P
